# Fritzing sketch Schematics (saved by Fritzing 0.9.2b)
breadboards: 1

parts:
  Part1 = Arduino Uno (Rev3)
  LED1 = LED - 5mm [color="Red (633nm)" package="5 mm [THT]"]
  LED2 = LED - 5mm [color="Red (633nm)" package="5 mm [THT]"]
  LED3 = LED - 5mm [color="Red (633nm)" package="5 mm [THT]"]
  LED4 = LED - 5mm [color="Red (633nm)" package="5 mm [THT]"]
  LED5 = LED - 5mm [color="Red (633nm)" package="5 mm [THT]"]
  LED6 = LED - 5mm [color="Red (633nm)" package="5 mm [THT]"]
  LED7 = LED - 5mm [color="Red (633nm)" package="5 mm [THT]"]
  LED8 = LED - 5mm [color="Red (633nm)" package="5 mm [THT]"]
  LED9 = LED - 5mm [color="Red (633nm)" package="5 mm [THT]"]

nets:
  N1: Part1.D8, LED1.cathode, LED5.cathode, LED8.cathode
  N2: Part1.D9_PWM, LED2.cathode, LED4.cathode, LED7.cathode
  N3: Part1.D10_PWM/SS, LED3.cathode, LED6.cathode, LED9.cathode
  N4: Part1.D3_PWM, LED7.anode, LED8.anode, LED9.anode
  N5: Part1.D4, LED4.anode, LED5.anode, LED6.anode
  N6: Part1.D5_PWM, LED1.anode, LED2.anode, LED3.anode
